# Fritzing sketch sun_tracker (saved by Fritzing 0.9.3b)
breadboards: 1

parts:
  U1 = NodeMCU V1.0
  PWM1 = PCA9685 16x12-bit PWM Breakout
  SERVO1 = Tower Pro SG90 servo [part_number=101246]
  SERVO2 = Tower Pro SG90 servo [part_number=101246]
  R1 = Photocell (LDR) [package=THT]
  R2 = Resistor [tolerance=±5% power=0.25 resistance=10k package=THT]

nets:
  N1: U1.D1, PWM1.no_name_yet#503
  N2: U1.D2, PWM1.no_name_yet#504
  +5V: U1.3V3, PWM1.no_name_yet#100, PWM1.no_name_yet#101, PWM1.no_name_yet#505, PWM1.no_name_yet#506, SERVO1.+5V, SERVO2.+5V, R1.pin_0
  GND: U1.GND, PWM1.no_name_yet#501, PWM1.no_name_yet#1000, PWM1.no_name_yet#1001, SERVO1.GND, SERVO2.GND, R2.Pin_1
  N3: U1.A0, R1.pin_1, R2.Pin_0
  N4: PWM1.no_name_yet#0, SERVO2.Signal
  N5: PWM1.no_name_yet#1, SERVO1.Signal

custom parts:
  NodeMCU V1.0: ESP8266 based NodeMCU
  Tower Pro SG90 servo: Original file by John De Cristofaro http://www.adafruit.com/products/1449 Adafruit Feedback Servo (Small) Edited by: e-radionica.com 28/9/2015
